# Fritzing sketch Lights-Numbers-With-LED (saved by Fritzing 0.9.3b)
circuit board: 5.94783cm x 5.20206cm
circuit board: 6.53358cm x 8.03576cm
circuit board: 5.93023cm x 5.19471cm
breadboards: 5

parts:
  IC005 = 74HC595 [package="DIP16 [THT]"]
  IC004 = 74HC595 [package="DIP16 [THT]"]
  IC001 = 74HC595 [package="DIP16 [THT]"]
  パーツ3 = Arduino Uno (Rev3)
  IC003 = 74HC595 [package="DIP16 [THT]"]
  IC002 = 74HC595 [package="DIP16 [THT]"]
  7_Segment_211 = 7 Segment Display
  7_Segment_213 = 7 Segment Display
  R203 = Resistor [tolerance=±5% resistance=220 package=THT]
  R215 = Resistor [tolerance=±5% resistance=220 package=THT]
  R204 = Resistor [tolerance=±5% resistance=220 package=THT]
  R216 = Resistor [tolerance=±5% resistance=220 package=THT]
  R205 = Resistor [tolerance=±5% resistance=220 package=THT]
  R217 = Resistor [tolerance=±5% resistance=220 package=THT]
  R206 = Resistor [tolerance=±5% resistance=220 package=THT]
  R218 = Resistor [tolerance=±5% resistance=220 package=THT]
  R201 = Resistor [tolerance=±5% resistance=220 package=THT]
  R213 = Resistor [tolerance=±5% resistance=220 package=THT]
  R202 = Resistor [tolerance=±5% resistance=220 package=THT]
  R214 = Resistor [tolerance=±5% resistance=220 package=THT]
  R207 = Resistor [tolerance=±5% resistance=220 package=THT]
  R211 = Resistor [tolerance=±5% resistance=220 package=THT]
  R208 = Resistor [tolerance=±5% resistance=220 package=THT]
  R212 = Resistor [tolerance=±5% resistance=220 package=THT]
  ULN2064B1 = ULN2064B [chip_label=ULN2064B package="DIP (Dual Inline) [THT]"]
  IC114 = ULN2064B [chip_label=ULN2064B package="DIP (Dual Inline) [THT]"]
  IC115 = ULN2064B [chip_label=ULN2064B package="DIP (Dual Inline) [THT]"]
  IC116 = ULN2064B [chip_label=ULN2064B package="DIP (Dual Inline) [THT]"]
  7_Segment_214 = 7 Segment Display
  7_Segment_215 = 7 Segment Display
  R221 = Resistor [tolerance=±5% resistance=220 package=THT]
  R222 = Resistor [tolerance=±5% resistance=220 package=THT]
  R223 = Resistor [tolerance=±5% resistance=220 package=THT]
  R224 = Resistor [tolerance=±5% resistance=220 package=THT]
  R225 = Resistor [tolerance=±5% resistance=220 package=THT]
  R226 = Resistor [tolerance=±5% resistance=220 package=THT]
  R227 = Resistor [tolerance=±5% resistance=220 package=THT]
  R228 = Resistor [tolerance=±5% resistance=220 package=THT]
  R229 = Resistor [tolerance=±5% resistance=220 package=THT]
  R231 = Resistor [tolerance=±5% resistance=220 package=THT]
  R232 = Resistor [tolerance=±5% resistance=220 package=THT]
  R234 = Resistor [tolerance=±5% resistance=220 package=THT]
  R235 = Resistor [tolerance=±5% resistance=220 package=THT]
  R236 = Resistor [tolerance=±5% resistance=220 package=THT]
  R238 = Resistor [tolerance=±5% resistance=220 package=THT]
  R239 = Resistor [tolerance=±5% resistance=220 package=THT]
  ULN2064B2 = ULN2064B [chip_label=ULN2064B package="DIP (Dual Inline) [THT]"]
  IC117 = ULN2064B [chip_label=ULN2064B package="DIP (Dual Inline) [THT]"]
  IC118 = ULN2064B [chip_label=ULN2064B package="DIP (Dual Inline) [THT]"]
  IC119 = ULN2064B [chip_label=ULN2064B package="DIP (Dual Inline) [THT]"]

nets:
  N1: IC005.Q1, IC118.pin14
  N2: IC005.Q2, IC119.pin3
  N3: IC005.Q3, IC119.pin5
  N4: IC005.Q4, IC119.pin11
  N5: IC005.Q5, IC119.pin14
  GND: IC005.GND, IC005.OE, IC004.GND, IC004.OE, IC001.GND, IC001.OE, パーツ3.GND, IC003.GND, IC003.OE, IC002.GND, IC002.OE, ULN2064B1.pin13, IC114.pin13, IC115.pin13, IC116.pin13
  VCC: IC005.MR, IC005.VCC, IC004.MR, IC004.VCC, IC001.MR, IC001.VCC, パーツ3.5V, IC003.MR, IC003.VCC, IC002.MR, IC002.VCC
  N6: IC005.SH_CP, IC004.SH_CP, IC001.SH_CP, パーツ3.D13/SCK, IC003.SH_CP, IC002.SH_CP
  N7: IC005.ST_CP, IC004.ST_CP, IC001.ST_CP, パーツ3.D10_PWM/SS, IC003.ST_CP, IC002.ST_CP
  N8: IC005.DS, IC004.Q7'
  N9: IC005.Q0, IC118.pin11
  N10: IC004.Q1, IC117.pin6
  N11: IC004.Q2, IC117.pin11
  N12: IC004.Q3, IC117.pin14
  N13: IC004.Q6, IC118.pin3
  N14: IC004.Q7, IC118.pin6
  N15: IC004.DS, IC003.Q7'
  N16: IC004.Q0, IC117.pin3
  N17: IC001.Q1, ULN2064B1.pin6
  N18: IC001.Q2, ULN2064B1.pin11
  N19: IC001.Q3, ULN2064B1.pin14
  N20: IC001.Q4, IC114.pin3
  N21: IC001.Q5, IC114.pin6
  N22: IC001.Q6, IC114.pin11
  N23: IC001.Q7, IC114.pin14
  N24: IC001.Q7', IC002.DS
  N25: IC001.DS, パーツ3.D11_PWM/MOSI
  N26: IC001.Q0, ULN2064B1.pin3
  N27: パーツ3.VIN, 7_Segment_211.common_anode, 7_Segment_213.common_anode, 7_Segment_214.common_anode, 7_Segment_215.common_anode
  N28: IC003.Q1, IC116.pin14
  N29: IC003.Q4, ULN2064B2.pin3
  N30: IC003.Q5, ULN2064B2.pin6
  N31: IC003.Q6, ULN2064B2.pin11
  N32: IC003.Q7, ULN2064B2.pin14
  N33: IC003.DS, IC002.Q7'
  N34: IC003.Q0, IC116.pin11
  N35: IC002.Q2, IC115.pin3
  N36: IC002.Q3, IC115.pin6
  N37: IC002.Q4, IC115.pin11
  N38: IC002.Q5, IC115.pin14
  N39: IC002.Q6, IC116.pin3
  N40: IC002.Q7, IC116.pin6
  N41: 7_Segment_211.Segment_E, R205.Pin_0
  N42: 7_Segment_211.Segment_D, R204.Pin_0
  N43: 7_Segment_211.Segment_C, R203.Pin_0
  N44: 7_Segment_211.Segment_DP, R208.Pin_0
  N45: 7_Segment_211.Segment_B, R202.Pin_0
  N46: 7_Segment_211.Segment_A, R201.Pin_0
  N47: 7_Segment_211.Segment_F, R206.Pin_0
  N48: 7_Segment_211.Segment_G, R207.Pin_0
  N49: 7_Segment_213.Segment_E, R215.Pin_0
  N50: 7_Segment_213.Segment_D, R214.Pin_0
  N51: 7_Segment_213.Segment_C, R213.Pin_0
  N52: 7_Segment_213.Segment_DP, R218.Pin_0
  N53: 7_Segment_213.Segment_B, R212.Pin_0
  N54: 7_Segment_213.Segment_A, R211.Pin_0
  N55: 7_Segment_213.Segment_F, R216.Pin_0
  N56: 7_Segment_213.Segment_G, R217.Pin_0
  N57: R203.Pin_1, ULN2064B1.pin9
  N58: R215.Pin_1, IC116.pin2
  N59: R204.Pin_1, ULN2064B1.pin16
  N60: R216.Pin_1, IC116.pin7
  N61: R205.Pin_1, IC114.pin2
  N62: R217.Pin_1, IC116.pin9
  N63: R206.Pin_1, IC114.pin7
  N64: R218.Pin_1, IC116.pin16
  N65: R201.Pin_1, ULN2064B1.pin2
  N66: R213.Pin_1, IC115.pin9
  N67: R202.Pin_1, ULN2064B1.pin7
  N68: R214.Pin_1, IC115.pin16
  N69: R207.Pin_1, IC114.pin9
  N70: R211.Pin_1, IC115.pin2
  N71: R208.Pin_1, IC114.pin16
  N72: R212.Pin_1, IC115.pin7
  N73: 7_Segment_214.Segment_E, R225.Pin_0
  N74: 7_Segment_214.Segment_D, R223.Pin_0
  N75: 7_Segment_214.Segment_C, R221.Pin_0
  N76: 7_Segment_214.Segment_DP, R238.Pin_0
  N77: 7_Segment_214.Segment_B, R232.Pin_0
  N78: 7_Segment_214.Segment_A, R229.Pin_0
  N79: 7_Segment_214.Segment_F, R227.Pin_0
  N80: 7_Segment_214.Segment_G, R235.Pin_0
  N81: 7_Segment_215.Segment_E, R222.Pin_0
  N82: 7_Segment_215.Segment_D, R234.Pin_0
  N83: 7_Segment_215.Segment_C, R231.Pin_0
  N84: 7_Segment_215.Segment_DP, R228.Pin_0
  N85: 7_Segment_215.Segment_B, R239.Pin_0
  N86: 7_Segment_215.Segment_A, R236.Pin_0
  N87: 7_Segment_215.Segment_F, R224.Pin_0
  N88: 7_Segment_215.Segment_G, R226.Pin_0
  N89: R221.Pin_1, ULN2064B2.pin9
  N90: R222.Pin_1, IC119.pin2
  N91: R223.Pin_1, ULN2064B2.pin16
  N92: R224.Pin_1, IC119.pin7
  N93: R225.Pin_1, IC117.pin2
  N94: R226.Pin_1, IC119.pin9
  N95: R227.Pin_1, IC117.pin7
  N96: R228.Pin_1, IC119.pin16
  N97: R229.Pin_1, ULN2064B2.pin2
  N98: R231.Pin_1, IC118.pin9
  N99: R232.Pin_1, ULN2064B2.pin7
  N100: R234.Pin_1, IC118.pin16
  N101: R235.Pin_1, IC117.pin9
  N102: R236.Pin_1, IC118.pin2
  N103: R238.Pin_1, IC117.pin16
  N104: R239.Pin_1, IC118.pin7
  N105: ULN2064B2.pin13, IC117.pin13, IC118.pin13, IC119.pin13

custom parts:
  ULN2064B: A DIP stand-in part for whatever IC you want. With 16 pins on a 300mil dual inline package (DIP) footprint.
